# Fritzing sketch ServoTest Sketch ESP32-S3 TFT (saved by Fritzing 0.9.10b)
breadboards: 1

parts:
  P1 = TRIMPOT [maximum_resistance=10kΩ knob_status=50% power=0.5W package=trimpot_pth_s3_lock]
  IC1_Level_Shifter = 74AHCT125 [part_number=SN74AHCT125 package=dil14]
  ServoL = Basic Servo
  ServoR = Basic Servo
  C1 = Electrolytic Capacitor [capacitance=1000µF voltage=25V package="300 mil [THT, electrolytic]"]
  MC1 = Adafruit ESP32-S3 TFT Feather [part_number="Adafruit #5483"]
  5v_DC = DC-DC Power Module (5v)
  S1 = Pushbutton [package="[THT]"]

nets:
  GND: P1.CCW, IC1_Level_Shifter.GND, IC1_Level_Shifter.3OE, IC1_Level_Shifter.4OE, ServoL.gnd, ServoR.gnd, C1.-, MC1.GND, 5v_DC.GND*
  N1: P1.WIPER, MC1.A5
  N2: P1.CW, MC1.3.3V, S1.Pin_1, S1.Pin_2
  N3: IC1_Level_Shifter.3Y, ServoR.pulse
  N4: IC1_Level_Shifter.3A, MC1.D12
  N5: IC1_Level_Shifter.4Y, ServoL.pulse
  N6: IC1_Level_Shifter.4A, MC1.D11
  VCC: IC1_Level_Shifter.VCC, ServoL.vcc, ServoR.vcc, C1.+, 5v_DC.Vout
  N7: MC1.D10, S1.Pin_3, S1.Pin_4

notes:
  Dual continuous rotation servos with speed and direction control & toggleable sticky stop

custom parts:
  74AHCT125: Quad Level-Shifter (3V to 5V) Quadruple Bus Buffer Gates With 3-State Outputs
  Adafruit ESP32-S3 TFT Feather: We've got a new machine here at Adafruit, it can uncover your deepest desires. Don't believe me? I'll turn it on right now to prove it to you! What, you want your very own soft serve ice cream machine? OK well, that's not something we can provide. But we can provide your second-deepest desire: an ESP32-S3 Feather board with a built in IPS TFT color display. It's got all the delicious creamy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
  DC-DC Power Module (5v): DC-DC Power Module based con AMS1117-5.0 Input: DC 6~12V (input power must higher 1V than output power); Output: 5V (+/-0.05V error), 800mA
