# Fritzing sketch QTPyRP2040HopeRF20230318 (saved by Fritzing 0.9.10b)
breadboards: 1

parts:
  Part1 = Adafruit QT Py RP2040 [part_number="Adafruit #4900"]
  RFM95W1 = RFM95W LoRa Module

nets:
  N1: Part1.+3V3, RFM95W1.13_3.3V
  N2: Part1.A2, RFM95W1.6_RESET
  N3: Part1.A3, RFM95W1.5_NSS_(CS)
  N4: Part1.SCK, RFM95W1.4_SCK
  N5: Part1.MISO, RFM95W1.2_MISO
  N6: Part1.MOSI, RFM95W1.3_MOSI
  N7: Part1.GND, RFM95W1.10_GND

custom parts:
  Adafruit QT Py RP2040: Description What a cutie pie! Or is it... a QT Py? This diminutive dev board comes with one of our new favorite chip, the RP2040. It's been made famous in the new Raspberry Pi Pico and our Feather RP2040 and ItsyBitsy RP2040, but what if we wanted something really smol? A new chip means a new QT Py, and the Raspberry Pi RP2040 is no exception. When we saw this chip we thought "this chip is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
  RFM95W LoRa Module: RF Transceiver by Hope RF. Well supported Arduino libraries are available. This Low Power Long Range Transceiver Module for the frequencies 868MHz and 915MHz and it is also available in other versions.
