# Fritzing sketch RPiPico_Thermistor_Piezo_LED_Button (saved by Fritzing 0.9.10b)
breadboards: 1

parts:
  Mod1 = Raspberry Pi Pico
  S1 = Pushbutton [package="[SMD]"]
  R1 = Resistor [tolerance=±5% resistance=10000 package="0402 [SMD]"]
  R2 = Temperature Sensor (Thermistor) [thermistor_type=NTC package=THT]
  J1 = Piezo Speaker

nets:
  N1: Mod1.pin_3, Mod1.pin_8, Mod1.pin_13, Mod1.pin_18, Mod1.pin_23, Mod1.pin_28, Mod1.pin_33, Mod1.pin_38, Mod1.pin_42, S1.Pin_1, S1.Pin_2, R2.pin_0, J1.pin1
  N2: Mod1.pin_7, S1.Pin_3, S1.Pin_4
  N3: Mod1.pin_21, J1.pin2
  N4: Mod1.pin_34, R1.Pin_1, R2.pin_1
  N5: Mod1.pin_36, R1.Pin_0

custom parts:
  Raspberry Pi Pico: Raspberry Pi Pico. Based around the RP2040 microcontroller the Pico is a low cost microcontroller device bringing Raspberry Pi quality, cost, and easy of use to the microcontroller space. Jan 2021, Split part in to two versions: tht (this one) and SMD. This one will drill holes for a .1 in header in pcb to allow plugging in the module as well as providing pads to solder the module to the top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
